// Logisim project project.circ as structural Verilog: 1 circuit, main circuit main
module main (
  input  in_1,
  input  in_2,
  input  in_3,
  input  in_4,
  input  in_5,
  output out_6,
  output out_7,
  output out_8,
  output out_9,
  output out_10
);

  wire and_1_out, not_1_out, or_1_out, or_2_out, or_3_out;

  and and_1 (and_1_out, in_2, in_3);
  or or_1 (or_1_out, in_2, in_3, in_4);
  or or_2 (or_2_out, and_1_out, in_4);
  not not_1 (not_1_out, out_6);
  and and_2 (out_7, in_1, or_1_out, not_1_out);
  and and_3 (out_6, in_1, or_2_out);
  or or_3 (or_3_out, out_7, out_6, in_5);
  not not_2 (out_9, or_3_out);
  or or_4 (out_10, out_6, in_5);

  assign out_8 = in_5;
endmodule
